// Logisim project arrondisseur.circ as structural Verilog: 1 circuit, main circuit main
module main (
  input  [13:0] M,
  output [9:0] out_2
);

  wire and_1_out, not_1_out, or_1_out;
  wire [1:0] and_2_out;
  wire [9:0] adder_1_out, multiplexer_1_out;

  and and_1 (and_1_out, M[3], 1'b1);
  or or_1 (or_1_out, M[0], M[1], M[2]);
  not not_1 (not_1_out, and_2_out[0]);
  and and_2 (and_2_out[0], and_1_out, or_1_out);
  Adder #(.width(10)) adder_1 (.a(M[13:4]), .b(10'h1), .out(adder_1_out));  // open: cin, cout
  Multiplexer #(.width(10)) multiplexer_1 (.in0(M[13:4]), .in1(adder_1_out), .out(multiplexer_1_out), .sel(M[4]));
  and and_3 (and_2_out[1], and_1_out, not_1_out);
  Multiplexer #(.select(2), .width(10)) multiplexer_2 (
    .in0(M[13:4]), .in1(adder_1_out), .in2(multiplexer_1_out), .out(out_2), .sel(and_2_out));  // open: in3
endmodule
