// Logisim project mips32B.circ as structural Verilog: 8 circuits, main circuit main
module main (
  input  EnBtn
);

  wire alu_1_zero, and_1_out, CLK_out, maincontrol_1_ainvert, maincontrol_1_alusrc, maincontrol_1_bnegate,
       maincontrol_1_branch, maincontrol_1_branchnot, maincontrol_1_extop, maincontrol_1_jump,
       maincontrol_1_memread, maincontrol_1_memtoreg, maincontrol_1_memwrite, maincontrol_1_regdst,
       maincontrol_1_regwrite, multiplexer_1_out, nand_1_out, Reset_out;
  wire [1:0] maincontrol_1_opr;
  wire [4:0] instructionsplitter_1_rd, instructionsplitter_1_rs, instructionsplitter_1_rt, multiplexer_2_out;
  wire [5:0] instructionsplitter_1_funct, instructionsplitter_1_opcode;
  wire [15:0] instructionsplitter_1_immediate;
  wire [25:0] instructionsplitter_1_target;
  wire [31:0] alu_1_result, bit_extender_1_out, bit_extender_2_out, multiplexer_3_out, multiplexer_4_out,
       multiplexer_5_out, pcunit_1_pc, ram_1_dout, regfile_1_output_1, regfile_1_output_2, rom_1_data;

  Clock CLK (.out(CLK_out));
  and and_1 (and_1_out, CLK_out, nand_1_out);
  Button Reset (.out(Reset_out));
  Multiplexer multiplexer_1 (.in0(pcunit_1_pc[22]), .in1(1'b1), .out(multiplexer_1_out), .sel(Reset_out));
  PCUnit pcunit_1 (
    .jump(maincontrol_1_jump), .target(instructionsplitter_1_target), .branchOffset(multiplexer_3_out),
    .branch(maincontrol_1_branch), .branchNot(maincontrol_1_branchnot), .zero(alu_1_zero), .enable(EnBtn),
    .clk(and_1_out), .reset(multiplexer_1_out), .pc(pcunit_1_pc));  // open: pc_plus_4
  ROM #(.addrWidth(5), .dataWidth(32)) rom_1 (.addr(pcunit_1_pc[6:2]), .data(rom_1_data));
  nand nand_1 (nand_1_out, rom_1_data[0], rom_1_data[1], rom_1_data[2], rom_1_data[3], rom_1_data[4], rom_1_data[5], rom_1_data[6], rom_1_data[7], rom_1_data[8], rom_1_data[9], rom_1_data[10], rom_1_data[11], rom_1_data[12], rom_1_data[13], rom_1_data[14], rom_1_data[15], rom_1_data[17], rom_1_data[18], rom_1_data[19], rom_1_data[20], rom_1_data[21], rom_1_data[22], rom_1_data[23], rom_1_data[24], rom_1_data[25], rom_1_data[26], rom_1_data[27], rom_1_data[28], rom_1_data[29], rom_1_data[30], rom_1_data[31], rom_1_data[16]);
  InstructionSplitter instructionsplitter_1 (
    .instruction(rom_1_data), .opcode(instructionsplitter_1_opcode), .rs(instructionsplitter_1_rs),
    .rt(instructionsplitter_1_rt), .rd(instructionsplitter_1_rd), .funct(instructionsplitter_1_funct),
    .immediate(instructionsplitter_1_immediate), .target(instructionsplitter_1_target));  // open: shamt
  Multiplexer #(.width(5)) multiplexer_2 (
    .in0(instructionsplitter_1_rt), .in1(instructionsplitter_1_rd), .out(multiplexer_2_out),
    .sel(maincontrol_1_regdst));
  MainControl maincontrol_1 (
    .opcode(instructionsplitter_1_opcode), .funct(instructionsplitter_1_funct),
    .RegWrite(maincontrol_1_regwrite), .RegDst(maincontrol_1_regdst), .ALUSrc(maincontrol_1_alusrc),
    .MemRead(maincontrol_1_memread), .MemWrite(maincontrol_1_memwrite), .MemToReg(maincontrol_1_memtoreg),
    .Branch(maincontrol_1_branch), .Jump(maincontrol_1_jump), .BranchNot(maincontrol_1_branchnot),
    .ExtOp(maincontrol_1_extop), .AInvert(maincontrol_1_ainvert), .Bnegate(maincontrol_1_bnegate),
    .OPR(maincontrol_1_opr));
  RegFile regfile_1 (
    .WriteData(multiplexer_5_out), .CLK(and_1_out), .RST(multiplexer_1_out),
    .RegWrite(maincontrol_1_regwrite), .WriteReg(multiplexer_2_out), .Read_Reg_1(instructionsplitter_1_rs),
    .Read_Reg_2(instructionsplitter_1_rt), .Output_1(regfile_1_output_1), .Output_2(regfile_1_output_2));
  assign bit_extender_1_out = {{16{instructionsplitter_1_immediate[15]}}, instructionsplitter_1_immediate};  // Bit_Extender bit_extender_1
  assign bit_extender_2_out = {{16{1'b0}}, instructionsplitter_1_immediate};  // Bit_Extender bit_extender_2
  Multiplexer #(.width(32)) multiplexer_3 (
    .in0(bit_extender_1_out), .in1(bit_extender_2_out), .out(multiplexer_3_out), .sel(maincontrol_1_extop));
  Multiplexer #(.width(32)) multiplexer_4 (
    .in0(regfile_1_output_2), .in1(multiplexer_3_out), .out(multiplexer_4_out), .sel(maincontrol_1_alusrc));
  ALU alu_1 (
    .AInvert(maincontrol_1_ainvert), .Bnegate(maincontrol_1_bnegate), .OPR(maincontrol_1_opr),
    .A(regfile_1_output_1), .B(multiplexer_4_out), .Result(alu_1_result), .Zero(alu_1_zero));  // open: OV_FLAG, Set_Flag, Cout
  RAM #(.addrWidth(24), .asyncread("true"), .clearpin("true"), .dataWidth(32)) ram_1 (
    .addr(alu_1_result[23:0]), .we(maincontrol_1_memwrite), .oe(maincontrol_1_memread), .clk(and_1_out),
    .din(regfile_1_output_2), .dout(ram_1_dout), .clr(multiplexer_1_out));
  Multiplexer #(.width(32)) multiplexer_5 (
    .in0(alu_1_result), .in1(ram_1_dout), .out(multiplexer_5_out), .sel(maincontrol_1_memtoreg));

  // Notes on the sheet:
  //   contents of rom_1 (hex, n*v repeats v):
  //   3408ffff 20090001 1095025 ac0a0000 8c0b0000 200c0005 200d0000 200e0000 1ac782a 11e00006 1ae7020
  //   21ce0001 15ccfffc ac0e0004 8c0f0004 1ec8022 12000002 20110037 8000014 2011007b ac110008 12a4824
  //   14b5025 16c5820 18d6022 1ae682a ac09000c ac0a0010 ac0b0014 ac0c0018 ac0d001c ac110020
endmodule

module RegFile (
  input  [31:0] WriteData,
  input  CLK,
  input  RST,
  input  RegWrite,
  input  [4:0] WriteReg,
  input  [4:0] Read_Reg_1,
  input  [4:0] Read_Reg_2,
  output [31:0] Output_1,
  output [31:0] Output_2
);

  wire decoder_1_out0, decoder_1_out1, decoder_1_out2, decoder_1_out3, decoder_1_out4, decoder_1_out5,
       decoder_1_out6, decoder_1_out7;
  wire [7:0] decoder_1_out8, decoder_1_out16, decoder_1_out24;
  wire [31:0] register_1_q, register_2_q, register_3_q, register_4_q, register_5_q, register_6_q,
       register_7_q, register_8_q, register_9_q, register_10_q, register_11_q, register_12_q, register_13_q,
       register_14_q, register_15_q, register_16_q, register_17_q, register_18_q, register_19_q,
       register_20_q, register_21_q, register_22_q, register_23_q, register_24_q, register_25_q,
       register_26_q, register_27_q, register_28_q, register_29_q, register_30_q, register_31_q,
       register_32_q;

  Decoder #(.select(5)) decoder_1 (
    .out0(decoder_1_out0), .out1(decoder_1_out1), .out2(decoder_1_out2), .out3(decoder_1_out3),
    .out4(decoder_1_out4), .out5(decoder_1_out5), .out6(decoder_1_out6), .out7(decoder_1_out7),
    .out8(decoder_1_out8[0]), .out9(decoder_1_out8[1]), .out10(decoder_1_out8[2]), .out11(decoder_1_out8[3]),
    .out12(decoder_1_out8[4]), .out13(decoder_1_out8[5]), .out14(decoder_1_out8[6]),
    .out15(decoder_1_out8[7]), .out16(decoder_1_out16[0]), .out17(decoder_1_out16[1]),
    .out18(decoder_1_out16[2]), .out19(decoder_1_out16[3]), .out20(decoder_1_out16[4]),
    .out21(decoder_1_out16[5]), .out22(decoder_1_out16[6]), .out23(decoder_1_out16[7]),
    .out24(decoder_1_out24[0]), .out25(decoder_1_out24[1]), .out26(decoder_1_out24[2]),
    .out27(decoder_1_out24[3]), .out28(decoder_1_out24[4]), .out29(decoder_1_out24[5]),
    .out30(decoder_1_out24[6]), .out31(decoder_1_out24[7]), .sel(WriteReg), .en(RegWrite));
  Register #(.width(32)) register_1 (.D(WriteData), .en(decoder_1_out0), .clk(CLK), .Q(register_1_q), .clr(RST));
  Register #(.width(32)) register_2 (.D(WriteData), .en(decoder_1_out1), .clk(CLK), .Q(register_2_q), .clr(RST));
  Register #(.width(32)) register_3 (.D(WriteData), .en(decoder_1_out2), .clk(CLK), .Q(register_3_q), .clr(RST));
  Register #(.width(32)) register_4 (.D(WriteData), .en(decoder_1_out3), .clk(CLK), .Q(register_4_q), .clr(RST));
  Register #(.width(32)) register_5 (.D(WriteData), .en(decoder_1_out4), .clk(CLK), .Q(register_5_q), .clr(RST));
  Register #(.width(32)) register_6 (.D(WriteData), .en(decoder_1_out5), .clk(CLK), .Q(register_6_q), .clr(RST));
  Register #(.width(32)) register_7 (.D(WriteData), .en(decoder_1_out6), .clk(CLK), .Q(register_7_q), .clr(RST));
  Register #(.width(32)) register_8 (.D(WriteData), .en(decoder_1_out7), .clk(CLK), .Q(register_8_q), .clr(RST));
  Register #(.width(32)) register_9 (.D(WriteData), .en(decoder_1_out8[0]), .clk(CLK), .Q(register_9_q), .clr(RST));
  Register #(.width(32)) register_10 (.D(WriteData), .en(decoder_1_out8[1]), .clk(CLK), .Q(register_10_q), .clr(RST));
  Register #(.width(32)) register_11 (.D(WriteData), .en(decoder_1_out8[2]), .clk(CLK), .Q(register_11_q), .clr(RST));
  Register #(.width(32)) register_12 (.D(WriteData), .en(decoder_1_out8[3]), .clk(CLK), .Q(register_12_q), .clr(RST));
  Register #(.width(32)) register_13 (.D(WriteData), .en(decoder_1_out8[4]), .clk(CLK), .Q(register_13_q), .clr(RST));
  Register #(.width(32)) register_14 (.D(WriteData), .en(decoder_1_out8[5]), .clk(CLK), .Q(register_14_q), .clr(RST));
  Register #(.width(32)) register_15 (.D(WriteData), .en(decoder_1_out8[6]), .clk(CLK), .Q(register_15_q), .clr(RST));
  Register #(.width(32)) register_16 (.D(WriteData), .en(decoder_1_out8[7]), .clk(CLK), .Q(register_16_q), .clr(RST));
  Register #(.width(32)) register_17 (.D(WriteData), .en(decoder_1_out16[0]), .clk(CLK), .Q(register_17_q), .clr(RST));
  Register #(.width(32)) register_18 (.D(WriteData), .en(decoder_1_out16[1]), .clk(CLK), .Q(register_18_q), .clr(RST));
  Register #(.width(32)) register_19 (.D(WriteData), .en(decoder_1_out16[2]), .clk(CLK), .Q(register_19_q), .clr(RST));
  Register #(.width(32)) register_20 (.D(WriteData), .en(decoder_1_out16[3]), .clk(CLK), .Q(register_20_q), .clr(RST));
  Register #(.width(32)) register_21 (.D(WriteData), .en(decoder_1_out16[4]), .clk(CLK), .Q(register_21_q), .clr(RST));
  Register #(.width(32)) register_22 (.D(WriteData), .en(decoder_1_out16[5]), .clk(CLK), .Q(register_22_q), .clr(RST));
  Register #(.width(32)) register_23 (.D(WriteData), .en(decoder_1_out16[6]), .clk(CLK), .Q(register_23_q), .clr(RST));
  Register #(.width(32)) register_24 (.D(WriteData), .en(decoder_1_out16[7]), .clk(CLK), .Q(register_24_q), .clr(RST));
  Register #(.width(32)) register_25 (.D(WriteData), .en(decoder_1_out24[0]), .clk(CLK), .Q(register_25_q), .clr(RST));
  Register #(.width(32)) register_26 (.D(WriteData), .en(decoder_1_out24[1]), .clk(CLK), .Q(register_26_q), .clr(RST));
  Register #(.width(32)) register_27 (.D(WriteData), .en(decoder_1_out24[2]), .clk(CLK), .Q(register_27_q), .clr(RST));
  Register #(.width(32)) register_28 (.D(WriteData), .en(decoder_1_out24[3]), .clk(CLK), .Q(register_28_q), .clr(RST));
  Register #(.width(32)) register_29 (.D(WriteData), .en(decoder_1_out24[4]), .clk(CLK), .Q(register_29_q), .clr(RST));
  Register #(.width(32)) register_30 (.D(WriteData), .en(decoder_1_out24[5]), .clk(CLK), .Q(register_30_q), .clr(RST));
  Register #(.width(32)) register_31 (.D(WriteData), .en(decoder_1_out24[6]), .clk(CLK), .Q(register_31_q), .clr(RST));
  Register #(.width(32)) register_32 (.D(WriteData), .en(decoder_1_out24[7]), .clk(CLK), .Q(register_32_q), .clr(RST));
  Multiplexer #(.select(5), .width(32)) multiplexer_1 (
    .in0(register_1_q), .in1(register_2_q), .in2(register_3_q), .in3(register_4_q), .in4(register_5_q),
    .in5(register_6_q), .in6(register_7_q), .in7(register_8_q), .in8(register_9_q), .in9(register_10_q),
    .in10(register_11_q), .in11(register_12_q), .in12(register_13_q), .in13(register_14_q),
    .in14(register_15_q), .in15(register_16_q), .in16(register_17_q), .in17(register_18_q),
    .in18(register_19_q), .in19(register_20_q), .in20(register_21_q), .in21(register_22_q),
    .in22(register_23_q), .in23(register_24_q), .in24(register_25_q), .in25(register_26_q),
    .in26(register_27_q), .in27(register_28_q), .in28(register_29_q), .in29(register_30_q),
    .in30(register_31_q), .in31(register_32_q), .out(Output_1), .sel(Read_Reg_1));
  Multiplexer #(.select(5), .width(32)) multiplexer_2 (
    .in0(register_1_q), .in1(register_2_q), .in2(register_3_q), .in3(register_4_q), .in4(register_5_q),
    .in5(register_6_q), .in6(register_7_q), .in7(register_8_q), .in8(register_9_q), .in9(register_10_q),
    .in10(register_11_q), .in11(register_12_q), .in12(register_13_q), .in13(register_14_q),
    .in14(register_15_q), .in15(register_16_q), .in16(register_17_q), .in17(register_18_q),
    .in18(register_19_q), .in19(register_20_q), .in20(register_21_q), .in21(register_22_q),
    .in22(register_23_q), .in23(register_24_q), .in24(register_25_q), .in25(register_26_q),
    .in26(register_27_q), .in27(register_28_q), .in28(register_29_q), .in29(register_30_q),
    .in30(register_31_q), .in31(register_32_q), .out(Output_2), .sel(Read_Reg_2));
endmodule

module MainControl (
  input  [5:0] opcode,
  input  [5:0] funct,
  output RegWrite,
  output RegDst,
  output ALUSrc,
  output MemRead,
  output MemWrite,
  output MemToReg,
  output Branch,
  output Jump,
  output BranchNot,
  output ExtOp,
  output AInvert,
  output Bnegate,
  output [1:0] OPR
);

  wire [10:9] rom_1_data;

  ROM #(.addrWidth(6), .dataWidth(12)) rom_1 (
    .addr(opcode),
    .data({ExtOp, rom_1_data, BranchNot, Jump, Branch, MemToReg, MemWrite, MemRead, ALUSrc, RegDst, RegWrite}));
  ALUControl alucontrol_1 (.funct(funct), .ALUOp(rom_1_data), .AInvert(AInvert), .Bnegate(Bnegate), .OPR(OPR));

  // Notes on the sheet:
  //   contents of rom_1 (hex, n*v repeats v):
  //   403 0 80 0 240 300 0 0 5 4*0 e05 21*0 2d 7*0 14
endmodule

module ALUControl (
  input  [5:0] funct,
  input  [1:0] ALUOp,
  output AInvert,
  output Bnegate,
  output [1:0] OPR
);

  ROM #(.dataWidth(4)) rom_1 (.addr({ALUOp, funct}), .data({AInvert, Bnegate, OPR}));

  // Notes on the sheet:
  //   contents of rom_1 (hex, n*v repeats v):
  //   64*2 64*6 32*0 2 0 6 0 0 1 4*0 7 21*0 64*1
endmodule

module ALU (
  input  AInvert,
  input  Bnegate,
  input  [1:0] OPR,
  input  [31:0] A,
  input  [31:0] B,
  output OV_FLAG,
  output Set_Flag,
  output Cout,
  output [31:0] Result,
  output Zero
);

  wire not_3_out, xor_1_out, xor_2_out;
  wire [31:0] adder_1_out, et_out, multiplexer_1_out, multiplexer_2_out, not_1_out, not_2_out, ou_out;

  Multiplexer #(.width(32)) multiplexer_1 (.in0(A), .in1(not_1_out), .out(multiplexer_1_out), .sel(AInvert));
  assign not_1_out = ~A;  // NOT_Gate not_1, 32 bits wide
  Multiplexer #(.width(32)) multiplexer_2 (.in0(B), .in1(not_2_out), .out(multiplexer_2_out), .sel(Bnegate));
  assign not_2_out = ~B;  // NOT_Gate not_2, 32 bits wide
  assign et_out = multiplexer_1_out & multiplexer_2_out;  // AND_Gate et, 32 bits wide
  assign ou_out = multiplexer_1_out | multiplexer_2_out;  // OR_Gate ou, 32 bits wide
  Adder #(.width(32)) adder_1 (
    .a(multiplexer_1_out), .b(multiplexer_2_out), .out(adder_1_out), .cin(Bnegate), .cout(Cout));
  xor xor_1 (xor_1_out, multiplexer_1_out[31], multiplexer_2_out[31]);
  not not_3 (not_3_out, xor_1_out);
  xor xor_2 (xor_2_out, multiplexer_1_out[31], adder_1_out[31]);
  xor xor_3 (Set_Flag, OV_FLAG, adder_1_out[31]);
  and and_1 (OV_FLAG, not_3_out, xor_2_out);
  Multiplexer #(.select(2), .width(32)) multiplexer_3 (
    .in0(et_out), .in1(ou_out), .in2(adder_1_out), .in3({{31{1'b0}}, Set_Flag}), .out(Result), .sel(OPR));
  Comparator #(.width(32)) comparator_1 (.a(Result), .b({32{1'b0}}), .eq(Zero));  // open: gt, lt

  // Notes on the sheet:
  //   less
  //   SLT_result
  //   AND_result
  //   OR_result
  //   ADD_result
endmodule

module JumpAddressGenerator (
  input  [31:0] PCPlus4,
  input  [25:0] target,
  output [31:0] JumpAddress
);


  assign JumpAddress = {PCPlus4[31:28], target, 2'b00};
endmodule

module InstructionSplitter (
  input  [31:0] instruction,
  output [5:0] opcode,
  output [4:0] rs,
  output [4:0] rt,
  output [4:0] rd,
  output [4:0] shamt,
  output [5:0] funct,
  output [15:0] immediate,
  output [25:0] target
);


  assign funct = instruction[5:0];
  assign immediate = instruction[15:0];
  assign opcode = instruction[31:26];
  assign rd = instruction[15:11];
  assign rs = instruction[25:21];
  assign rt = instruction[20:16];
  assign shamt = instruction[10:6];
  assign target = instruction[25:0];
endmodule

module PCUnit (
  input  jump,
  input  [25:0] target,
  input  [31:0] branchOffset,
  input  branch,
  input  branchNot,
  input  zero,
  input  enable,
  input  clk,
  input  reset,
  output [31:0] pc,
  output [31:0] pc_plus_4
);

  wire and_1_out, and_2_out, not_1_out, or_1_out;
  wire [31:0] adder_1_out, adder_2_out, jumpaddressgenerator_1_jumpaddress, multiplexer_2_out, shifter_1_out;

  Register #(.width(32)) register_1 (.D(pc_plus_4), .en(enable), .clk(clk), .Q(pc), .clr(reset));
  Multiplexer #(.width(32)) multiplexer_1 (
    .in0(multiplexer_2_out), .in1(jumpaddressgenerator_1_jumpaddress), .out(pc_plus_4), .sel(jump));
  Adder #(.width(32)) adder_1 (.a(pc), .b(32'h4), .out(adder_1_out));  // open: cin, cout
  JumpAddressGenerator jumpaddressgenerator_1 (
    .PCPlus4(multiplexer_2_out), .target(target), .JumpAddress(jumpaddressgenerator_1_jumpaddress));
  Shifter #(.width(32)) shifter_1 (.in(branchOffset), .\dist (5'b00010), .out(shifter_1_out));
  Adder #(.width(32)) adder_2 (.a(adder_1_out), .b(shifter_1_out), .out(adder_2_out));  // open: cin, cout
  Multiplexer #(.width(32)) multiplexer_2 (
    .in0(adder_1_out), .in1(adder_2_out), .out(multiplexer_2_out), .sel(or_1_out));
  or or_1 (or_1_out, and_1_out, and_2_out);
  and and_1 (and_1_out, branch, zero);
  and and_2 (and_2_out, branchNot, not_1_out);
  not not_1 (not_1_out, zero);
endmodule
